# Fritzing sketch MPS20N0040D Pressure Sensor - Raspberry Pi (saved by Fritzing 0.9.3b)
breadboards: 1

parts:
  Part1 = Adafruit ADS1115 16Bit I2C ADC [part_number="Adafruit #1085"]
  IC2 = DIP - 6 pins [chip_label=MPS package="DIP (Dual Inline) [THT]"]
  Raspberry_Pi_1 = Raspberry Pi 3 [part_number=RPI-3-V1.2]

nets:
  VCC: Part1.AIN2, Part1.AIN1, IC2.VCC, Raspberry_Pi_1.3v3
  GND: Part1.AIN0, Part1.ADDR, IC2.GND, Raspberry_Pi_1.GND

custom parts:
  Adafruit ADS1115 16Bit I2C ADC: For microcontrollers without an analog-to-digital converter or when you want a higher-precision ADC, the ADS1115 provides 16-bit precision at 860 samples/second over I2C. The chip can be configured as 4 single-ended input channels, or two differential channels. As a nice bonus, it even includes a programmable gain amplifier, up to x16, to help boost up smaller single/differential signals to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
  DIP - 6 pins: A DIP stand-in part for whatever IC you want. With 6 pins on a 300mil dual inline package (DIP) footprint.
